// Logisim project TP1.circ as structural Verilog: 5 circuits, main circuit main
module main (
  input  INVA,
  input  ENA,
  input  ENB,
  input  A0,
  input  B0,
  input  Carry_in,
  input  A1,
  input  B1,
  input  A2,
  input  B2,
  input  F0,
  input  F1,
  output S0,
  output S1,
  output S2,
  output Carry_out
);

  wire alu1bit_1_carry_out, alu1bit_2_carry_out;

  ALU1bit alu1bit_1 (
    .INVA(INVA), .A(A0), .ENA(ENA), .B(B0), .ENB(ENB), .F0(F0), .F1(F1), .Carry_in(Carry_in),
    .Carry_out(alu1bit_1_carry_out), .Output(S0));
  ALU1bit alu1bit_2 (
    .INVA(INVA), .A(A1), .ENA(ENA), .B(B1), .ENB(ENB), .F0(F0), .F1(F1), .Carry_in(alu1bit_1_carry_out),
    .Carry_out(alu1bit_2_carry_out), .Output(S1));
  ALU1bit alu1bit_3 (
    .INVA(INVA), .A(A2), .ENA(ENA), .B(B2), .ENB(ENB), .F0(F0), .F1(F1), .Carry_in(alu1bit_2_carry_out),
    .Carry_out(Carry_out), .Output(S2));
endmodule

module Decoder (
  input  F0,
  input  F1,
  output S0,
  output S1,
  output S2,
  output S3
);

  wire not_1_out, not_2_out, not_3_out, not_4_out;

  not not_1 (not_1_out, F0);
  not not_2 (not_2_out, F1);
  not not_3 (not_3_out, F0);
  not not_4 (not_4_out, F1);
  and and_1 (S0, not_1_out, not_2_out);
  and and_2 (S1, not_3_out, F1);
  and and_3 (S2, F0, not_4_out);
  and and_4 (S3, F0, F1);
endmodule

module FullAdder (
  input  Carry_in,
  input  B,
  input  A,
  input  Enable,
  output Sum,
  output Carry_out
);

  wire and_1_out, and_2_out, xor_1_out, xor_2_out;

  and and_1 (and_1_out, Enable, A, B);
  or or_1 (Carry_out, and_1_out, and_2_out);
  xor xor_1 (xor_1_out, B, A);
  and and_2 (and_2_out, Enable, xor_1_out, Carry_in);
  xor xor_2 (xor_2_out, Carry_in, xor_1_out);
  and and_3 (Sum, xor_2_out, Enable);
endmodule

module LogicalUnit (
  input  A,
  input  B,
  input  Enable_AB,
  input  Enable_A_B,
  input  Enable_Not_B,
  output AB,
  output A_B,
  output Not_B
);

  wire A_B_out, AB_out, Not_B_out;

  and u_AB (AB_out, A, B);
  or u_A_B (A_B_out, A, B);
  not u_Not_B (Not_B_out, B);
  and and_1 (AB, AB_out, Enable_AB);
  and and_2 (A_B, A_B_out, Enable_A_B);
  and and_3 (Not_B, Not_B_out, Enable_Not_B);
endmodule

module ALU1bit (
  input  Carry_in,
  input  INVA,
  input  A,
  input  ENA,
  input  B,
  input  ENB,
  input  F0,
  input  F1,
  output Output,
  output Carry_out
);

  wire and_1_out, and_2_out, Decoder_s0, Decoder_s1, Decoder_s2, Decoder_s3, Full_adder_sum,
       Logical_unit_a_b, Logical_unit_ab, Logical_unit_not_b, xor_1_out;

  and and_1 (and_1_out, A, ENA);
  and and_2 (and_2_out, B, ENB);
  xor xor_1 (xor_1_out, INVA, and_1_out);
  Decoder Decoder (.F0(F0), .F1(F1), .S0(Decoder_s0), .S1(Decoder_s1), .S2(Decoder_s2), .S3(Decoder_s3));
  LogicalUnit Logical_unit (
    .A(xor_1_out), .B(and_2_out), .Enable_AB(Decoder_s0), .Enable_A_B(Decoder_s1), .Enable_Not_B(Decoder_s2),
    .AB(Logical_unit_ab), .A_B(Logical_unit_a_b), .Not_B(Logical_unit_not_b));
  FullAdder Full_adder (
    .B(and_2_out), .A(xor_1_out), .Enable(Decoder_s3), .Carry_in(Carry_in), .Carry_out(Carry_out),
    .Sum(Full_adder_sum));
  or or_1 (Output, Logical_unit_ab, Logical_unit_a_b, Logical_unit_not_b, Full_adder_sum);

  // Notes on the sheet:
  //   Sum
endmodule
