// Logisim project TP2.circ as structural Verilog: 8 circuits, main circuit main
module main (
  input  INVA,
  input  ENA,
  input  ENB,
  input  A0,
  input  B0,
  input  Carry_in,
  input  A1,
  input  B1,
  input  A2,
  input  B2,
  input  F0,
  input  F1,
  output S0,
  output S1,
  output S2,
  output Carry_out
);

  wire alu1bit_1_carry_out, alu1bit_2_carry_out;

  ALU1bit alu1bit_1 (
    .INVA(INVA), .A(A0), .ENA(ENA), .B(B0), .ENB(ENB), .F0(F0), .F1(F1), .Carry_in(Carry_in),
    .Carry_out(alu1bit_1_carry_out), .Output(S0));
  ALU1bit alu1bit_2 (
    .INVA(INVA), .A(A1), .ENA(ENA), .B(B1), .ENB(ENB), .F0(F0), .F1(F1), .Carry_in(alu1bit_1_carry_out),
    .Carry_out(alu1bit_2_carry_out), .Output(S1));
  ALU1bit alu1bit_3 (
    .INVA(INVA), .A(A2), .ENA(ENA), .B(B2), .ENB(ENB), .F0(F0), .F1(F1), .Carry_in(alu1bit_2_carry_out),
    .Carry_out(Carry_out), .Output(S2));
endmodule

module Decoder (
  input  F0,
  input  F1,
  output S0,
  output S1,
  output S2,
  output S3
);

  wire not_1_out, not_2_out, not_3_out, not_4_out;

  not not_1 (not_1_out, F0);
  not not_2 (not_2_out, F1);
  not not_3 (not_3_out, F0);
  not not_4 (not_4_out, F1);
  and and_1 (S0, not_1_out, not_2_out);
  and and_2 (S1, not_3_out, F1);
  and and_3 (S2, F0, not_4_out);
  and and_4 (S3, F0, F1);
endmodule

module FullAdder (
  input  Carry_in,
  input  B,
  input  A,
  input  Enable,
  output Sum,
  output Carry_out
);

  wire and_1_out, and_2_out, xor_1_out, xor_2_out;

  and and_1 (and_1_out, Enable, A, B);
  or or_1 (Carry_out, and_1_out, and_2_out);
  xor xor_1 (xor_1_out, B, A);
  and and_2 (and_2_out, Enable, xor_1_out, Carry_in);
  xor xor_2 (xor_2_out, Carry_in, xor_1_out);
  and and_3 (Sum, xor_2_out, Enable);
endmodule

module LogicalUnit (
  input  A,
  input  B,
  input  Enable_AB,
  input  Enable_A_B,
  input  Enable_Not_B,
  output AB,
  output A_B,
  output Not_B
);

  wire A_B_out, AB_out, Not_B_out;

  and u_AB (AB_out, A, B);
  or u_A_B (A_B_out, A, B);
  not u_Not_B (Not_B_out, B);
  and and_1 (AB, AB_out, Enable_AB);
  and and_2 (A_B, A_B_out, Enable_A_B);
  and and_3 (Not_B, Not_B_out, Enable_Not_B);
endmodule

module ALU1bit (
  input  Carry_in,
  input  INVA,
  input  A,
  input  ENA,
  input  B,
  input  ENB,
  input  F0,
  input  F1,
  output Output,
  output Carry_out
);

  wire and_1_out, and_2_out, Decoder_s0, Decoder_s1, Decoder_s2, Decoder_s3, Full_adder_sum,
       Logical_unit_a_b, Logical_unit_ab, Logical_unit_not_b, xor_1_out;

  and and_1 (and_1_out, A, ENA);
  and and_2 (and_2_out, B, ENB);
  xor xor_1 (xor_1_out, INVA, and_1_out);
  Decoder Decoder (.F0(F0), .F1(F1), .S0(Decoder_s0), .S1(Decoder_s1), .S2(Decoder_s2), .S3(Decoder_s3));
  LogicalUnit Logical_unit (
    .A(xor_1_out), .B(and_2_out), .Enable_AB(Decoder_s0), .Enable_A_B(Decoder_s1), .Enable_Not_B(Decoder_s2),
    .AB(Logical_unit_ab), .A_B(Logical_unit_a_b), .Not_B(Logical_unit_not_b));
  FullAdder Full_adder (
    .B(and_2_out), .A(xor_1_out), .Enable(Decoder_s3), .Carry_in(Carry_in), .Carry_out(Carry_out),
    .Sum(Full_adder_sum));
  or or_1 (Output, Logical_unit_ab, Logical_unit_a_b, Logical_unit_not_b, Full_adder_sum);

  // Notes on the sheet:
  //   Sum
endmodule

module Mult3bits (
  input  A2,
  input  A1,
  input  A0,
  input  B2,
  input  B1,
  input  B0,
  output S5,
  output S4,
  output S3,
  output S2,
  output S1,
  output S0
);

  wire and_1_out, and_2_out, and_3_out, and_4_out, and_5_out, and_6_out, and_7_out, and_8_out, C0_out,
       C1_out, C2_out, C3_out, C4_out, C5_out, C6_out, C7_out, C8_out, C9_out, C10_out, C11_out, xor_1_out,
       xor_2_out, xor_3_out, xor_5_out, xor_6_out, xor_8_out, xor_9_out, xor_10_out;

  or or_1 (S5, C8_out, C9_out, C10_out, C11_out);
  and C8 (C8_out, and_1_out, C4_out);
  and C9 (C9_out, xor_1_out, C5_out);
  and C10 (C10_out, xor_2_out, C6_out);
  and C11 (C11_out, xor_3_out, C7_out);
  and and_1 (and_1_out, A2, B2);
  xor xor_1 (xor_1_out, and_1_out, C4_out);
  and C4 (C4_out, and_2_out, and_3_out);
  and C5 (C5_out, C1_out, C2_out);
  xor xor_2 (xor_2_out, xor_1_out, C5_out);
  and C6 (C6_out, xor_5_out, xor_8_out);
  xor xor_3 (xor_3_out, xor_2_out, C6_out);
  and C7 (C7_out, xor_6_out, C3_out);
  xor xor_4 (S4, xor_3_out, C7_out);
  and and_2 (and_2_out, A1, B2);
  xor xor_5 (xor_5_out, and_2_out, and_3_out);
  xor xor_6 (xor_6_out, xor_5_out, xor_8_out);
  xor xor_7 (S3, xor_6_out, C3_out);
  and and_3 (and_3_out, A2, B1);
  and and_4 (and_4_out, A0, B2);
  and C1 (C1_out, and_4_out, and_6_out);
  and C2 (C2_out, and_5_out, C0_out);
  xor xor_8 (xor_8_out, C1_out, C2_out);
  and C3 (C3_out, xor_10_out, xor_9_out);
  and and_5 (and_5_out, A2, B0);
  and and_6 (and_6_out, A1, B1);
  xor xor_9 (xor_9_out, and_5_out, C0_out);
  xor xor_10 (xor_10_out, and_4_out, and_6_out);
  xor xor_11 (S2, xor_10_out, xor_9_out);
  and C0 (C0_out, and_7_out, and_8_out);
  and and_7 (and_7_out, A0, B1);
  and and_8 (and_8_out, A1, B0);
  xor xor_12 (S1, and_7_out, and_8_out);
  and and_9 (S0, A0, B0);
endmodule

module Mult3bits_V2 (
  input  A2,
  input  A1,
  input  A0,
  input  B2,
  input  B1,
  input  B0,
  output S5,
  output S4,
  output S3,
  output S2,
  output S1,
  output S0
);

  wire B0A1_out, B0A2_out, B1A0_out, B1A1_out, B1A2_out, B2A0_out, B2A1_out, B2A2_out, fulladder_2_carry_out,
       fulladder_2_sum, fulladder_3_carry_out, fulladder_4_carry_out, fulladder_5_carry_out, fulladder_5_sum,
       fulladder_6_carry_out;

  and B2A2 (B2A2_out, A2, B2);
  FullAdder fulladder_1 (
    .B(fulladder_2_carry_out), .A(B2A2_out), .Enable(1'b1), .Carry_in(fulladder_3_carry_out), .Carry_out(S5),
    .Sum(S4));
  and B1A2 (B1A2_out, A2, B1);
  and B2A1 (B2A1_out, A1, B2);
  FullAdder fulladder_2 (
    .B(B1A2_out), .A(B2A1_out), .Enable(1'b1), .Carry_in(fulladder_5_carry_out),
    .Carry_out(fulladder_2_carry_out), .Sum(fulladder_2_sum));
  FullAdder fulladder_3 (
    .B(fulladder_4_carry_out), .A(fulladder_2_sum), .Enable(1'b1), .Carry_in(1'b0),
    .Carry_out(fulladder_3_carry_out), .Sum(S3));
  and B1A1 (B1A1_out, A1, B1);
  and B2A0 (B2A0_out, A0, B2);
  FullAdder fulladder_4 (
    .B(fulladder_5_sum), .A(B2A0_out), .Enable(1'b1), .Carry_in(1'b0), .Carry_out(fulladder_4_carry_out),
    .Sum(S2));
  and B0A2 (B0A2_out, A2, B0);
  FullAdder fulladder_5 (
    .B(B0A2_out), .A(B1A1_out), .Enable(1'b1), .Carry_in(fulladder_6_carry_out),
    .Carry_out(fulladder_5_carry_out), .Sum(fulladder_5_sum));
  and B1A0 (B1A0_out, A0, B1);
  FullAdder fulladder_6 (
    .B(B0A1_out), .A(B1A0_out), .Enable(1'b1), .Carry_in(1'b0), .Carry_out(fulladder_6_carry_out), .Sum(S1));
  and B0A1 (B0A1_out, A1, B0);
  and B0A0 (S0, A0, B0);
endmodule

module Add3bits (
  input  A0,
  input  A0_2,
  input  A0_3,
  input  B2,
  input  B1,
  input  B0,
  output Carry_out,
  output S3,
  output S1,
  output S0
);

  wire fulladder_2_carry_out, fulladder_3_carry_out;

  FullAdder fulladder_1 (
    .B(B2), .A(A0), .Enable(1'b1), .Carry_in(fulladder_2_carry_out), .Carry_out(Carry_out), .Sum(S3));
  FullAdder fulladder_2 (
    .B(B1), .A(A0_2), .Enable(1'b1), .Carry_in(fulladder_3_carry_out), .Carry_out(fulladder_2_carry_out),
    .Sum(S1));
  FullAdder fulladder_3 (.B(B0), .A(A0_3), .Enable(1'b1), .Carry_in(1'b0), .Carry_out(fulladder_3_carry_out), .Sum(S0));
endmodule
